# Fritzing sketch bluetooth car (saved by Fritzing 0.9.3b)

parts:
  Parça1 = Arduino Uno (Rev3)
  S1 = H-Bridge with L298N
  VCC1 = 4 x AAA Battery Mount
  Parça2 = Bluetooth HC-05 Macho
  M1 = DC Motor
  M2 = DC Motor

nets:
  GND: Parça1.GND, S1.GND, VCC1.-, Parça2.GND
  N1: Parça1.D0/RX, Parça2.TXD
  N2: Parça1.D1/TX, Parça2.RXD
  N3: Parça1.D2, S1.IN1
  N4: Parça1.D3_PWM, S1.IN2
  N5: Parça1.D4, S1.IN3
  N6: Parça1.D5_PWM, S1.IN4
  3V3: Parça1.3V3, Parça2.VCC
  VIN: Parça1.VIN, S1.5V
  N7: S1.12V, VCC1.+
  N8: S1.M1-01, M2.pin_1
  N9: S1.M1-02, M2.pin_2
  N10: S1.M2-01, M1.pin_1
  N11: S1.M2-02, M1.pin_2

custom parts:
  H-Bridge with L298N: h-bridge

// code stored in the sketch: Untitled.ino
#include <SoftwareSerial.h>
SoftwareSerial bluetooth(0,1);
int okunanKarakter;
int in1 = 2;
int in2 = 3;
int in3 = 4;
int in4 = 5;
int trigger = 8;
int echo = 10;
int mesafe;
int sure;
/*Kodun Setup Ba?lang?c?---------------------------------------------------------------------------------------------------------------------------------------------------------------*/
void setup() {
    pinMode(in1,OUTPUT);
    pinMode(in2,OUTPUT);
    pinMode(in3,OUTPUT);
    pinMode(in4,OUTPUT);
    pinMode(trigger,OUTPUT);
    pinMode(echo,INPUT);
    bluetooth.begin(9600);
    
}
/*Kodun Loop Ba?lang?c?----------------------------------------------------------------------------------------------------------------------------------------------------------------*/
void loop() {
  digitalWrite(trigger,HIGH);
  delayMicroseconds(1000);
  digitalWrite(trigger,LOW);
  sure = pulseIn(echo,HIGH);
  mesafe = (sure/2) / 29.1;
  if(mesafe < 1)
  {
  digitalWrite(in1,HIGH);
  digitalWrite(in2,HIGH);
  digitalWrite(in3,HIGH);
  digitalWrite(in4,HIGH);
  }
  while(bluetooth.available()>0){ /* Yeni veri var m? */
    okunanKarakter = bluetooth.read(); /* Yeni veriyi okunanKarakter degiskenine kaydet */
    switch(okunanKarakter){ /* Okunan karaktere göre i?lem yap */
      case 'a': /* gelen karakterin i?lem kar??l??? */
    digitalWrite(in1,HIGH);
    digitalWrite(in2,LOW);
    digitalWrite(in3,HIGH);
    digitalWrite(in4,LOW);

        bluetooth.println("?leri");
        break;
      case 'b': 
        digitalWrite(in1,LOW);
        digitalWrite(in2,HIGH);
        digitalWrite(in3,LOW);
        digitalWrite(in4,HIGH);

        bluetooth.println("Geri");
        break;  
      case 'c':
        digitalWrite(in1,HIGH);
        digitalWrite(in2,LOW);
        digitalWrite(in3,LOW);
        digitalWrite(in4,LOW);
        bluetooth.println("Sa?a Dönü?");
        break;
      case 'd':
        digitalWrite(in1,LOW);
        digitalWrite(in2,LOW);
        digitalWrite(in3,HIGH);
        digitalWrite(in4,LOW);
     
        bluetooth.println("Sola Dönü?");
        break;
      case 'e':
        digitalWrite(in1,HIGH);
        digitalWrite(in2,HIGH);
        digitalWrite(in3,HIGH);
        digitalWrite(in4,HIGH);
        bluetooth.println("Dur");
       break;
    } /* Switch sonu */
  }/* While sonu*/
}/*Kodun Sonu-----------------------------------------------------------------------------------------------------------------------------------------------------------------------------------------*/
